// Logisim project cpu.circ as structural Verilog: 15 circuits, main circuit DLatch
module main (
  input  reset,
  output [15:0] out_2
);

  wire and_1_out, clock_1_out, Cntrl_isimmediate, Cntrl_jump, Cntrl_readmem, Cntrl_writeenable,
       Cntrl_writemem, decode_negative, not_1_out, not_2_out, not_3_out, not_4_out, not_5_out, or_1_out,
       or_2_out;
  wire [1:0] Cntrl_aluselect;
  wire [3:0] controlled_buffer_1_out, controlled_buffer_2_out, controlled_buffer_4_out,
       controlled_buffer_5_out, decode_imm, decode_opcode, decode_reg0, decode_src1, decode_src2;
  wire [7:0] controlled_buffer_3_out, decode_addr;
  wire [9:0] n10bitextender_1_out_2;
  wire [11:0] decode_jmpaddr;
  wire [15:0] _16eXT_out_2, alu_out_4, controlled_buffer_7_out, multiplexer_1_out, multiplexer_2_out,
       n4bitext_1_jmpaddrout, pc_1_out_5, ram_1_data, registerfile_1_output1, registerfile_1_output2,
       rom_1_data;

  Clock clock_1 (.out(clock_1_out));
  pc pc_1 (.reset(reset), .clk(clock_1_out), .jmpAddr(n4bitext_1_jmpaddrout), .jmp(Cntrl_jump), .out_5(pc_1_out_5));
  _4bitExt u_4bitext_1 (.jmpAddrIn(decode_jmpaddr), .isSigned(decode_negative), .jmpAddrOut(n4bitext_1_jmpaddrout));
  ROM #(.addrWidth(16), .dataWidth(16)) rom_1 (.addr(pc_1_out_5), .data(rom_1_data), .sel(1'b1));
  decode decode (
    .instruction(rom_1_data), .src2(decode_src2), .imm(decode_imm), .src1(decode_src1), .addr(decode_addr),
    .jmpAddr(decode_jmpaddr), .negative(decode_negative), .reg0(decode_reg0), .opcode(decode_opcode));
  assign controlled_buffer_1_out = Cntrl_isimmediate ? decode_imm : 4'bz;  // Controlled_Buffer controlled_buffer_1
  control Cntrl (
    .opcode(decode_opcode), .reset(clock_1_out), .aluselect(Cntrl_aluselect),
    .isImmediate(Cntrl_isimmediate), .writeEnable(Cntrl_writeenable), .readMem(Cntrl_readmem),
    .writeMem(Cntrl_writemem), .jump(Cntrl_jump));
  assign controlled_buffer_2_out = not_1_out ? decode_reg0 : 4'bz;  // Controlled_Buffer controlled_buffer_2
  assign controlled_buffer_3_out = or_1_out ? decode_addr : 8'bz;  // Controlled_Buffer controlled_buffer_3
  or or_1 (or_1_out, Cntrl_readmem, Cntrl_writemem);
  not not_1 (not_1_out, Cntrl_writemem);
  assign controlled_buffer_4_out = and_1_out ? decode_src2 : 4'bz;  // Controlled_Buffer controlled_buffer_4
  and and_1 (and_1_out, not_3_out, not_4_out);
  assign controlled_buffer_5_out = not_2_out ? decode_src1 : 4'bz;  // Controlled_Buffer controlled_buffer_5
  not not_2 (not_2_out, or_2_out);
  not not_3 (not_3_out, or_2_out);
  not not_4 (not_4_out, Cntrl_isimmediate);
  or or_2 (or_2_out, Cntrl_readmem, Cntrl_writemem);
  registerFile registerfile_1 (
    .Clk(clock_1_out), .reg2(controlled_buffer_4_out), .wrR(controlled_buffer_2_out),
    .WriteEnable(Cntrl_writeenable), .\input (multiplexer_1_out), .reset(reset),
    .output1(registerfile_1_output1), .reg1(controlled_buffer_5_out), .output2(registerfile_1_output2));
  assign controlled_buffer_5_out = Cntrl_writemem ? decode_reg0 : 4'bz;  // Controlled_Buffer controlled_buffer_6
  Multiplexer #(.width(16)) multiplexer_1 (
    .in0(out_2), .in1(ram_1_data), .out(multiplexer_1_out), .sel(Cntrl_readmem));  // open: en
  _10bitExtender u_10bitextender_1 (.in_1(controlled_buffer_3_out), .out_2(n10bitextender_1_out_2));
  _16bitExtender _16eXT (.in_1(controlled_buffer_1_out), .out_2(_16eXT_out_2));
  not not_5 (not_5_out, Cntrl_readmem);
  Multiplexer #(.width(16)) multiplexer_2 (
    .in0(registerfile_1_output2), .in1(_16eXT_out_2), .out(multiplexer_2_out), .sel(Cntrl_isimmediate));  // open: en
  assign controlled_buffer_7_out = not_5_out ? registerfile_1_output1 : 16'bz;  // Controlled_Buffer controlled_buffer_7
  alu alu (.input1(registerfile_1_output1), .input2(multiplexer_2_out), .aluselect(Cntrl_aluselect), .out_4(alu_out_4));
  Multiplexer #(.width(16)) multiplexer_3 (
    .in0(alu_out_4), .in1({16{1'b0}}), .out(out_2), .sel(clock_1_out));  // open: en
  RAM #(.addrWidth(10), .dataWidth(16), .bus("separate")) ram_1 (
    .addr(n10bitextender_1_out_2), .din(controlled_buffer_7_out), .data(ram_1_data), .str(Cntrl_writemem),
    .sel(1'b1), .clk(clock_1_out), .ld(Cntrl_readmem), .clr(reset));

  // Notes on the sheet:
  //   contents of rom_1 (hex, n*v repeats v):
  //   7000 7102 7303 4210 413 820a 552c 2601 3713 6ff5
endmodule

module DLatch (
  input  D,
  input  C,
  input  reset,
  output out_4,
  output Q_prime
);

  wire nand_1_out, nand_2_out, not_1_out, not_2_out;

  not not_1 (not_1_out, D);
  nand nand_1 (nand_1_out, D, C);
  nand nand_2 (nand_2_out, C, not_1_out);
  not not_2 (not_2_out, reset);
  nand nand_3 (out_4, nand_1_out, Q_prime);
  nand nand_4 (Q_prime, out_4, nand_2_out, not_2_out);
endmodule

module DFlipFlop (
  input  Clk,
  input  D,
  input  reset,
  output Q
);

  wire dlatch_1_out_4, not_1_out;

  not not_1 (not_1_out, Clk);
  DLatch dlatch_1 (.D(D), .C(not_1_out), .reset(reset), .out_4(dlatch_1_out_4));  // open: Q_prime
  DLatch dlatch_2 (.D(dlatch_1_out_4), .C(Clk), .reset(reset), .out_4(Q));  // open: Q_prime
endmodule

module _16BitRegister (
  input  reset,
  input  Clk,
  input  [15:0] \input ,
  output [15:0] \output 
);

  DFlipFlop dflipflop_1 (.Clk(Clk), .D(\input [0]), .reset(reset), .Q(\output [0]));
  DFlipFlop dflipflop_2 (.Clk(Clk), .D(\input [1]), .reset(reset), .Q(\output [1]));
  DFlipFlop dflipflop_3 (.Clk(Clk), .D(\input [2]), .reset(reset), .Q(\output [2]));
  DFlipFlop dflipflop_4 (.Clk(Clk), .D(\input [3]), .reset(reset), .Q(\output [3]));
  DFlipFlop dflipflop_5 (.Clk(Clk), .D(\input [4]), .reset(reset), .Q(\output [4]));
  DFlipFlop dflipflop_6 (.Clk(Clk), .D(\input [5]), .reset(reset), .Q(\output [5]));
  DFlipFlop dflipflop_7 (.Clk(Clk), .D(\input [6]), .reset(reset), .Q(\output [6]));
  DFlipFlop dflipflop_8 (.Clk(Clk), .D(\input [7]), .reset(reset), .Q(\output [7]));
  DFlipFlop dflipflop_9 (.Clk(Clk), .D(\input [8]), .reset(reset), .Q(\output [8]));
  DFlipFlop dflipflop_10 (.Clk(Clk), .D(\input [9]), .reset(reset), .Q(\output [9]));
  DFlipFlop dflipflop_11 (.Clk(Clk), .D(\input [10]), .reset(reset), .Q(\output [10]));
  DFlipFlop dflipflop_12 (.Clk(Clk), .D(\input [11]), .reset(reset), .Q(\output [11]));
  DFlipFlop dflipflop_13 (.Clk(Clk), .D(\input [12]), .reset(reset), .Q(\output [12]));
  DFlipFlop dflipflop_14 (.Clk(Clk), .D(\input [13]), .reset(reset), .Q(\output [13]));
  DFlipFlop dflipflop_15 (.Clk(Clk), .D(\input [14]), .reset(reset), .Q(\output [14]));
  DFlipFlop dflipflop_16 (.Clk(Clk), .D(\input [15]), .reset(reset), .Q(\output [15]));
endmodule

module registerFile (
  input  [15:0] \input ,
  input  Clk,
  input  reset,
  input  [3:0] reg1,
  input  [3:0] reg2,
  input  [3:0] wrR,
  input  WriteEnable,
  output [15:0] output1,
  output [15:0] output2
);

  wire and_1_out, and_2_out, and_3_out, and_4_out, and_5_out, and_6_out, and_7_out, and_8_out, and_9_out,
       and_10_out, and_11_out, and_12_out, and_13_out, and_14_out, and_15_out, and_16_out, and_17_out,
       and_18_out, and_19_out, and_20_out, and_21_out, and_22_out, and_23_out, and_24_out, and_25_out,
       and_26_out, and_27_out, and_28_out, and_29_out, and_30_out, and_31_out, and_32_out, decoder_1_out0,
       decoder_1_out1, decoder_1_out2, decoder_1_out3, decoder_1_out4, decoder_1_out5, decoder_1_out6,
       decoder_1_out7, decoder_1_out8, decoder_1_out9, decoder_1_out10, decoder_1_out11, decoder_1_out12,
       decoder_1_out13, decoder_1_out14, decoder_1_out15;
  wire [15:0] n16bitregister_1_output, n16bitregister_2_output, n16bitregister_3_output,
       n16bitregister_4_output, n16bitregister_5_output, n16bitregister_6_output, n16bitregister_7_output,
       n16bitregister_8_output, n16bitregister_9_output, n16bitregister_10_output, n16bitregister_11_output,
       n16bitregister_12_output, n16bitregister_13_output, n16bitregister_14_output,
       n16bitregister_15_output, n16bitregister_16_output;

  Decoder #(.select(4)) decoder_1 (
    .out0(decoder_1_out0), .out1(decoder_1_out1), .out2(decoder_1_out2), .out3(decoder_1_out3),
    .out4(decoder_1_out4), .out5(decoder_1_out5), .out6(decoder_1_out6), .out7(decoder_1_out7),
    .out8(decoder_1_out8), .out9(decoder_1_out9), .out10(decoder_1_out10), .out11(decoder_1_out11),
    .out12(decoder_1_out12), .out13(decoder_1_out13), .out14(decoder_1_out14), .out15(decoder_1_out15),
    .sel(wrR));  // open: en
  and and_1 (and_1_out, decoder_1_out0, WriteEnable);
  and and_2 (and_2_out, decoder_1_out1, WriteEnable);
  and and_3 (and_3_out, decoder_1_out2, WriteEnable);
  and and_4 (and_4_out, decoder_1_out3, WriteEnable);
  and and_5 (and_5_out, decoder_1_out4, WriteEnable);
  and and_6 (and_6_out, decoder_1_out5, WriteEnable);
  and and_7 (and_7_out, decoder_1_out6, WriteEnable);
  and and_8 (and_8_out, decoder_1_out7, WriteEnable);
  and and_9 (and_9_out, decoder_1_out8, WriteEnable);
  and and_10 (and_10_out, decoder_1_out9, WriteEnable);
  and and_11 (and_11_out, decoder_1_out10, WriteEnable);
  and and_12 (and_12_out, decoder_1_out11, WriteEnable);
  and and_13 (and_13_out, decoder_1_out12, WriteEnable);
  and and_14 (and_14_out, decoder_1_out13, WriteEnable);
  and and_15 (and_15_out, decoder_1_out14, WriteEnable);
  and and_16 (and_16_out, decoder_1_out15, WriteEnable);
  and and_17 (and_17_out, Clk, and_1_out);
  and and_18 (and_18_out, Clk, and_2_out);
  and and_19 (and_19_out, Clk, and_3_out);
  and and_20 (and_20_out, Clk, and_4_out);
  and and_21 (and_21_out, Clk, and_5_out);
  and and_22 (and_22_out, Clk, and_6_out);
  and and_23 (and_23_out, Clk, and_7_out);
  and and_24 (and_24_out, Clk, and_8_out);
  and and_25 (and_25_out, Clk, and_9_out);
  and and_26 (and_26_out, Clk, and_10_out);
  and and_27 (and_27_out, Clk, and_11_out);
  and and_28 (and_28_out, Clk, and_12_out);
  and and_29 (and_29_out, Clk, and_13_out);
  and and_30 (and_30_out, Clk, and_14_out);
  and and_31 (and_31_out, Clk, and_15_out);
  and and_32 (and_32_out, Clk, and_16_out);
  _16BitRegister u_16bitregister_1 (
    .Clk(and_17_out), .\input (\input ), .reset(reset), .\output (n16bitregister_1_output));
  _16BitRegister u_16bitregister_2 (
    .Clk(and_18_out), .\input (\input ), .reset(reset), .\output (n16bitregister_2_output));
  _16BitRegister u_16bitregister_3 (
    .Clk(and_19_out), .\input (\input ), .reset(reset), .\output (n16bitregister_3_output));
  _16BitRegister u_16bitregister_4 (
    .Clk(and_20_out), .\input (\input ), .reset(reset), .\output (n16bitregister_4_output));
  _16BitRegister u_16bitregister_5 (
    .Clk(and_21_out), .\input (\input ), .reset(reset), .\output (n16bitregister_5_output));
  _16BitRegister u_16bitregister_6 (
    .Clk(and_22_out), .\input (\input ), .reset(reset), .\output (n16bitregister_6_output));
  _16BitRegister u_16bitregister_7 (
    .Clk(and_23_out), .\input (\input ), .reset(reset), .\output (n16bitregister_7_output));
  _16BitRegister u_16bitregister_8 (
    .Clk(and_24_out), .\input (\input ), .reset(reset), .\output (n16bitregister_8_output));
  _16BitRegister u_16bitregister_9 (
    .Clk(and_25_out), .\input (\input ), .reset(reset), .\output (n16bitregister_9_output));
  _16BitRegister u_16bitregister_10 (
    .Clk(and_26_out), .\input (\input ), .reset(reset), .\output (n16bitregister_10_output));
  _16BitRegister u_16bitregister_11 (
    .Clk(and_27_out), .\input (\input ), .reset(reset), .\output (n16bitregister_11_output));
  _16BitRegister u_16bitregister_12 (
    .Clk(and_28_out), .\input (\input ), .reset(reset), .\output (n16bitregister_12_output));
  _16BitRegister u_16bitregister_13 (
    .Clk(and_29_out), .\input (\input ), .reset(reset), .\output (n16bitregister_13_output));
  _16BitRegister u_16bitregister_14 (
    .Clk(and_30_out), .\input (\input ), .reset(reset), .\output (n16bitregister_14_output));
  _16BitRegister u_16bitregister_15 (
    .Clk(and_31_out), .\input (\input ), .reset(reset), .\output (n16bitregister_15_output));
  _16BitRegister u_16bitregister_16 (
    .Clk(and_32_out), .\input (\input ), .reset(reset), .\output (n16bitregister_16_output));
  Multiplexer #(.select(4), .width(16), .enable("false")) multiplexer_1 (
    .in0(n16bitregister_1_output), .in1(n16bitregister_2_output), .in2(n16bitregister_3_output),
    .in3(n16bitregister_4_output), .in4(n16bitregister_5_output), .in5(n16bitregister_6_output),
    .in6(n16bitregister_7_output), .in7(n16bitregister_8_output), .in8(n16bitregister_9_output),
    .in9(n16bitregister_10_output), .in10(n16bitregister_11_output), .in11(n16bitregister_12_output),
    .in12(n16bitregister_13_output), .in13(n16bitregister_14_output), .in14(n16bitregister_15_output),
    .in15(n16bitregister_16_output), .out(output1), .sel(reg1));
  Multiplexer #(.select(4), .width(16), .enable("false")) multiplexer_2 (
    .in0(n16bitregister_1_output), .in1(n16bitregister_2_output), .in2(n16bitregister_3_output),
    .in3(n16bitregister_4_output), .in4(n16bitregister_5_output), .in5(n16bitregister_6_output),
    .in6(n16bitregister_7_output), .in7(n16bitregister_8_output), .in8(n16bitregister_9_output),
    .in9(n16bitregister_10_output), .in10(n16bitregister_11_output), .in11(n16bitregister_12_output),
    .in12(n16bitregister_13_output), .in13(n16bitregister_14_output), .in14(n16bitregister_15_output),
    .in15(n16bitregister_16_output), .out(output2), .sel(reg2));
endmodule

module decode (
  input  [15:0] instruction,
  output [3:0] src2,
  output [3:0] imm,
  output [3:0] src1,
  output [7:0] addr,
  output [11:0] jmpAddr,
  output negative,
  output [3:0] reg0,
  output [3:0] opcode
);


  assign addr = instruction[7:0];
  assign imm = instruction[3:0];
  assign jmpAddr = instruction[11:0];
  assign negative = instruction[11];
  assign opcode = instruction[15:12];
  assign reg0 = instruction[11:8];
  assign src1 = instruction[7:4];
  assign src2 = instruction[3:0];
endmodule

module alu (
  input  [15:0] input1,
  input  [15:0] input2,
  input  [1:0] aluselect,
  output [15:0] out_4
);

  wire [15:0] add_1_out_3, and_1_out, or_1_out;

  assign or_1_out = input1 | input2;  // OR_Gate or_1, 16 bits wide
  assign and_1_out = input1 & input2;  // AND_Gate and_1, 16 bits wide
  add add_1 (.input1(input1), .input2(input2), .out_3(add_1_out_3));
  Multiplexer #(.select(2), .width(16)) multiplexer_1 (
    .in0(or_1_out), .in1(and_1_out), .in2(add_1_out_3), .out(out_4), .sel(aluselect));  // open: in3, en
endmodule

module fulladder (
  input  a,
  input  b,
  input  ci,
  output s,
  output CO
);

  wire and_1_out, and_2_out, and_3_out;

  and and_1 (and_1_out, a, b);
  and and_2 (and_2_out, a, ci);
  and and_3 (and_3_out, b, ci);
  ExactlyOne xor_1 (.out(s), .in0(a), .in1(b), .in2(ci));
  or or_1 (CO, and_1_out, and_2_out, and_3_out);
endmodule

module add (
  input  [15:0] input1,
  input  [15:0] input2,
  output [15:0] out_3
);

  wire fulladder_1_co, fulladder_2_co, fulladder_3_co, fulladder_4_co, fulladder_5_co, fulladder_6_co,
       fulladder_7_co, fulladder_8_co, fulladder_9_co, fulladder_10_co, fulladder_11_co, fulladder_12_co,
       fulladder_13_co, fulladder_14_co, halfadder_1_co;

  halfadder halfadder_1 (.a(input1[0]), .b(input2[0]), .s(out_3[0]), .CO(halfadder_1_co));
  fulladder fulladder_1 (.a(input1[1]), .b(input2[1]), .ci(halfadder_1_co), .s(out_3[1]), .CO(fulladder_1_co));
  fulladder fulladder_2 (.a(input1[2]), .b(input2[2]), .ci(fulladder_1_co), .s(out_3[2]), .CO(fulladder_2_co));
  fulladder fulladder_3 (.a(input1[3]), .b(input2[3]), .ci(fulladder_2_co), .s(out_3[3]), .CO(fulladder_3_co));
  fulladder fulladder_4 (.a(input1[4]), .b(input2[4]), .ci(fulladder_3_co), .s(out_3[4]), .CO(fulladder_4_co));
  fulladder fulladder_5 (.a(input1[5]), .b(input2[5]), .ci(fulladder_4_co), .s(out_3[5]), .CO(fulladder_5_co));
  fulladder fulladder_6 (.a(input1[6]), .b(input2[6]), .ci(fulladder_5_co), .s(out_3[6]), .CO(fulladder_6_co));
  fulladder fulladder_7 (.a(input1[7]), .b(input2[7]), .ci(fulladder_6_co), .s(out_3[7]), .CO(fulladder_7_co));
  fulladder fulladder_8 (.a(input1[8]), .b(input2[8]), .ci(fulladder_7_co), .s(out_3[8]), .CO(fulladder_8_co));
  fulladder fulladder_9 (.a(input1[9]), .b(input2[9]), .ci(fulladder_8_co), .s(out_3[9]), .CO(fulladder_9_co));
  fulladder fulladder_10 (.a(input1[10]), .b(input2[10]), .ci(fulladder_9_co), .s(out_3[10]), .CO(fulladder_10_co));
  fulladder fulladder_11 (.a(input1[11]), .b(input2[11]), .ci(fulladder_10_co), .s(out_3[11]), .CO(fulladder_11_co));
  fulladder fulladder_12 (.a(input1[12]), .b(input2[12]), .ci(fulladder_11_co), .s(out_3[12]), .CO(fulladder_12_co));
  fulladder fulladder_13 (.a(input1[13]), .b(input2[13]), .ci(fulladder_12_co), .s(out_3[13]), .CO(fulladder_13_co));
  fulladder fulladder_14 (.a(input1[14]), .b(input2[14]), .ci(fulladder_13_co), .s(out_3[14]), .CO(fulladder_14_co));
  fulladder fulladder_15 (.a(input1[15]), .b(input2[15]), .ci(fulladder_14_co), .s(out_3[15]));  // open: CO
endmodule

module halfadder (
  input  a,
  input  b,
  output s,
  output CO
);

  xor xor_1 (s, a, b);
  and and_1 (CO, a, b);
endmodule

module control (
  input  [3:0] opcode,
  input  reset,
  output [1:0] aluselect,
  output isImmediate,
  output writeEnable,
  output readMem,
  output writeMem,
  output jump
);

  wire decoder_1_out0, decoder_1_out1, decoder_1_out2, decoder_1_out3, decoder_1_out4, decoder_1_out5;
  wire [2:0] or_3_out;
  wire [3:0] multiplexer_1_out;

  Decoder #(.select(4)) decoder_1 (
    .out0(decoder_1_out0), .out1(decoder_1_out1), .out2(decoder_1_out2), .out3(decoder_1_out3),
    .out4(decoder_1_out4), .out5(decoder_1_out5), .out6(jump), .out7(readMem), .out8(writeMem),
    .sel(multiplexer_1_out));  // open: out9, out10, out11, out12, out13, out14, out15, en
  Multiplexer #(.width(4)) multiplexer_1 (
    .in0(opcode), .in1(4'b1111), .out(multiplexer_1_out), .sel(reset));  // open: en
  or or_1 (or_3_out[2], decoder_1_out0, decoder_1_out1);
  or or_2 (or_3_out[1], decoder_1_out2, decoder_1_out3);
  or or_3 (or_3_out[0], decoder_1_out4, decoder_1_out5);
  or or_4 (writeEnable, decoder_1_out5, decoder_1_out4, decoder_1_out3, decoder_1_out2, decoder_1_out1, decoder_1_out0, readMem);
  or or_5 (isImmediate, decoder_1_out3, decoder_1_out1, decoder_1_out5);
  Multiplexer #(.select(3), .width(2)) multiplexer_2 (
    .in1(2'b10), .in2(2'b01), .in4(2'b00), .out(aluselect), .sel(or_3_out));  // open: in0, in3, in5, in6, in7, en
endmodule

module _16bitExtender (
  input  [3:0] in_1,
  output [15:0] out_2
);


  assign out_2 = {{12{1'b0}}, in_1};
endmodule

module pc (
  input  reset,
  input  clk,
  input  [15:0] jmpAddr,
  input  jmp,
  output [15:0] out_5
);

  wire [15:0] add_1_out_3, multiplexer_1_out;

  Multiplexer #(.width(16)) multiplexer_1 (.in0(16'h1), .in1(jmpAddr), .out(multiplexer_1_out), .sel(jmp));  // open: en
  add add_1 (.input1(out_5), .input2(multiplexer_1_out), .out_3(add_1_out_3));
  _16BitRegister u_16bitregister_1 (.Clk(clk), .\input (add_1_out_3), .reset(reset), .\output (out_5));
endmodule

module _10bitExtender (
  input  [7:0] in_1,
  output [9:0] out_2
);


  assign out_2 = {2'b00, in_1};
endmodule

module _4bitExt (
  input  [11:0] jmpAddrIn,
  input  isSigned,
  output [15:0] jmpAddrOut
);

  Multiplexer #(.width(4)) multiplexer_1 (
    .in0(4'b0000), .in1(4'b1111), .out(jmpAddrOut[15:12]), .sel(isSigned));  // open: en

  assign jmpAddrOut[11:0] = jmpAddrIn;
endmodule
